# Fritzing sketch ckt (saved by Fritzing 0.9.3b)
breadboards: 2

parts:
  M1 = 7in-display [package=THT]
  Mod1 = gy-906
  M2 = MakerFocus MAX30102
  Part2 = Adafruit VL530X Time of Flight Distance Sensor [part_number="Adafruit #3317"]
  SEN1 = Pulse Sensor [package=SIP-3]
  power_supply = bb-usb-cable [package=THT]  # not connected
  A1 = Sparkfun load cell amplifier
  S1 = Load Sensor - 50kg [part_number=SEN-10245]
  S2 = Load Sensor - 50kg [part_number=SEN-10245]
  Mod2 = Raspberry Pi 4B
  U1 = ESP32-38PinWide [part_number=ESP32-38PinWide]
  Part3 = Flat Ribbon
  S3 = Load Sensor - 50kg [part_number=SEN-10245]
  S4 = Load Sensor - 50kg [part_number=SEN-10245]

nets:
  VSS: M1.VSS, A1.Pin_9, Mod2.5V, U1.VIN, Part3.Pin_0, Part3.Pin_12
  N1: M1.SCL, Mod2.GPIO2
  N2: M1.SDO, Mod2.GPIO3
  N3: M1.NC, Mod2.GND
  N4: M1.VDD, Part3.Pin_1, Part3.Pin_13
  N5: M1./RD, Part3.Pin_2, Part3.Pin_14
  N6: M1./WR, Part3.Pin_3, Part3.Pin_15
  N7: M1./CS, Part3.Pin_4, Part3.Pin_16
  N8: M1.RS, Part3.Pin_5, Part3.Pin_17
  N9: M1.DB0, Part3.Pin_6, Part3.Pin_18
  N10: M1.DB1, Part3.Pin_7, Part3.Pin_19
  N11: M1.DB3, Part3.Pin_8, Part3.Pin_20
  N12: M1./INT, Part3.Pin_9, Part3.Pin_21
  N13: M1.TP_BUSY, Part3.Pin_10, Part3.Pin_22
  N14: M1.TP_INT, Part3.Pin_11, Part3.Pin_23
  N15: Mod1.SCL, U1.GPIO18
  N16: Mod1.SDA, U1.GPIO19
  N17: M2.SCL, U1.GPIO21
  N18: M2.SDA, U1.GPIO22
  N19: Part2.SCL, U1.GPIO26
  N20: Part2.SDA, U1.GPIO25
  GND: SEN1.GND, U1.GND
  N21: SEN1.VCC, U1.3.3
  N22: SEN1.Signal, U1.GPIO34
  N23: A1.Pin_1, S4.R
  N24: A1.Pin_2, S3.R
  N25: A1.Pin_3, S2.R
  N26: A1.Pin_4, S1.R
  N27: A1.Pin_6, Mod2.3V3, U1.GPIO11
  N28: A1.Pin_7, U1.GPIO5
  N29: A1.Pin_8, U1.GPIO4
  N30: S1.B, S4.B
  N31: S1.W, S2.W
  N32: S2.B, S3.B
  N33: Mod2.GPIO14, U1.GPIO17
  N34: Mod2.GPIO15, U1.GPIO9
  N35: S3.W, S4.W

custom parts:
  7in-display: 7In tft rgb touch screen display.
  gy-906: gy-906 Non-contact PIR I2C interface temperature sensor breakout board.
  MakerFocus MAX30102: Oximeter module using the MAX30102 chip. As usual, if you want the mounting holes in pcb, you need to drag a hole over the pad in silkscreen to actually drill the hole (by default they are not drilled)
  Adafruit VL530X Time of Flight Distance Sensor: The VL53L0X is a Time of Flight distance sensor like no other you've used! The sensor contains a very tiny invisible laser source, and a matching sensor. The VL53L0X can detect the "time of flight", or how long the light has taken to bounce back to the sensor. Since it uses a very narrow light source, it is good for determining distance of only the surface directly in front of it. Unlike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
  Pulse Sensor: Pulse Sensor Optical Heart Beat Sensor
  bb-usb-cable: Breadboard only, no connectors USB cable for the Raspberry PIs.
  Sparkfun load cell amplifier: The SparkFun Load Cell Amplifier is a small breakout board for the HX711 IC that allows you to easily read load cells to measure weight.
  Load Sensor - 50kg: Half-wheatstone bridge Load Cell modified from the Fritzing Repo This load sensor, sometimes called a strain gauge, is the same one found in digital bathroom scales (you know, the ones you use in January for your New Year's resolutions, and then forget about a month later). This sensor can measure up to about 110 pounds.
  ESP32-38PinWide: Generic 38-Pin ESP32 with wide format (only access to one side of pins on a breadboard) based on Stephen Lilley's HiLetgo ESP-WROOM-32 ESP32 ESP-32S Development Board.
